# Fritzing sketch circuit (saved by Fritzing 0.9.3b)
breadboards: 1

parts:
  JL012-13-5_1 = JL012-13-5.2 Lever (Limit) Switch SPDT + NO + NC [part_number=JL012-13-5.2]
  Part2 = INMP441
  A2 = olimex ESP32-POE-ISO
  M1 = BME680 Module [part_number=CJMCU-680]
  A3 = PMS5003
  A4 = LD2410
  M2 = CK-07 [package=THT]

nets:
  N1: JL012-13-5_1.C, A2.Pin_19
  GND: JL012-13-5_1.NO, Part2.GND, A2.Pin_3, A2.Pin_32, M1.GND, A3.Pin_2, A4.Pin_4, M2.pin_2, M2.pin_3
  N2: Part2.L/R, Part2.WS, A2.Pin_14
  N3: Part2.SCK, A2.Pin_17
  N4: Part2.SD, A2.Pin_18
  VDD: Part2.VDD, A2.Pin_2, A2.Pin_31, M1.VCC, M2.pin_4
  N5: A2.Pin_1, A3.Pin_1, A4.Pin_5
  N6: A2.Pin_9, A2.Pin_30, A4.Pin_3
  N7: A2.Pin_10, A4.Pin_2
  N8: A2.Pin_11, A2.Pin_12
  N9: A2.Pin_13, M1.SDA
  N10: A2.Pin_15, A3.Pin_4
  N11: A2.Pin_16, M1.SCL
  N12: A2.Pin_21, M2.pin_1
  N13: A2.Pin_22, A3.Pin_5

notes:
  Limit Switch
  SCD40-CO2 Sensor
  BME680
  Temp/Humidity/Pressure/Altitude
  INMP441
  PIR Mini
  LDR Module
  ESP32-POE
  Air Quality PM2.5 Sensor
  Microwave Radar Sensor

custom parts:
  JL012-13-5.2 Lever (Limit) Switch SPDT + NO + NC: Micro Switch; Model No.: JL012-13.5-2; Actuator Action: Momentary; Actuator Type: Hinge Lever; Contact Configuration: 1NO, 1NC (SPDT) Temperature -25~65℃；Relative humidity: below 85%; Rate Voltage: 125V AC; Rated Current: 1A.
  INMP441: This is a simple breakout board for the INMP441 I2S MEMS microphone.
  olimex ESP32-POE-ISO: ESP32-PoE is an IoT WIFI/BLE/Ethernet development board with Power-Over-Ethernet feature.
  BME680 Module: Bosch BME680 Development Module The BME680 is a digital 4-in-1 sensor that measures air quality [gas], humidity, pressure and temperature. Links: BME680 product datasheet
  PMS5003: PMS5003 is a kind of digital and universal particle concentration sensor, which can be used to obtain the number of suspended particles in the air.
  LD2410: LD2410 is a high-sensitivity 24GHz human presence status sensing module developed by Hi-link.
  CK-07: Fc-51 Infrared Obstacle Avoidance Proximity Sensor module. IR transmitter led, receiver LED, lm393 compaitor and a pot. 3.3 V to 5V power.
