# Fritzing sketch schematics (saved by Fritzing 0.9.3b)
breadboards: 1

parts:
  JL012-13-5_1 = JL012-13-5.2 Lever (Limit) Switch SPDT + NO + NC [part_number=JL012-13-5.2]
  A1 = ENS160 AHT21
  Part1 = BME280
  Part2 = INMP441
  A2 = olimex ESP32-POE-ISO
  PIR1 = PIR sensor

nets:
  N1: JL012-13-5_1.C, A2.Pin_19
  GND: JL012-13-5_1.NO, A1.Pin_3, Part1.GND, Part2.GND, A2.Pin_32, PIR1.GND
  N2: A1.Pin_1, Part2.VDD, A2.Pin_2, A2.Pin_31
  N3: A1.Pin_4, Part1.SCL, A2.Pin_16
  N4: A1.Pin_5, Part1.SDA, A2.Pin_13
  VIN: Part1.VIN, PIR1.VDD
  N5: Part2.L/R, Part2.WS, A2.Pin_14, A2.Pin_23
  N6: Part2.SCK, A2.Pin_17
  N7: Part2.SD, A2.Pin_18
  N8: A2.Pin_8, PIR1.SIG
  N9: A2.Pin_11, A2.Pin_12

notes:
  Limit Switch
  ENS160 Multi-gas sensor
  BME280
  INMP441
  PIR Mini
  LDR Module
  ESP32-POE

custom parts:
  JL012-13-5.2 Lever (Limit) Switch SPDT + NO + NC: Micro Switch; Model No.: JL012-13.5-2; Actuator Action: Momentary; Actuator Type: Hinge Lever; Contact Configuration: 1NO, 1NC (SPDT) Temperature -25~65℃；Relative humidity: below 85%; Rate Voltage: 125V AC; Rated Current: 1A.
  ENS160 AHT21: The CO2 Gas- Air- Sensor is based on ENS160 in combination with an AHT21 Temperature Humidity Sensor.
  INMP441: This is a simple breakout board for the INMP441 I2S MEMS microphone.
  olimex ESP32-POE-ISO: ESP32-PoE is an IoT WIFI/BLE/Ethernet development board with Power-Over-Ethernet feature.
